// Logisim project adder2.circ as structural Verilog: 2 circuits, main circuit full_adder
module full_adder (
  input  A,
  input  B,
  input  Cin,
  output S,
  output Cout
);

  wire and_1_out, and_2_out, undriven, undriven_2, undriven_3, undriven_4, xor_1_out;

  xor xor_1 (xor_1_out, undriven, undriven_2);
  and and_1 (and_1_out, A, B);
  xor xor_2 (S, undriven_3, undriven_4);
  and and_2 (and_2_out, Cin, xor_1_out);
  or or_1 (Cout, and_1_out, and_2_out);
endmodule

module adder2 (
  input  A1,
  input  A0,
  input  B1,
  input  B0,
  output S0,
  output S1,
  output C
);

  wire fa0_cout;

  full_adder fa0 (.A(A0), .B(B0), .Cin(1'b0), .S(S0), .Cout(fa0_cout));
  full_adder fa1 (.A(A1), .B(B1), .Cin(fa0_cout), .S(S1), .Cout(C));
endmodule
