// Logisim project cmos.circ as structural Verilog: 4 circuits, main circuit cmos_inv
module cmos_inv (
  input  A,
  output Y
);

  wire undriven;

  Transistor #(.\type ("p")) transistor_1 (.in(1'b1), .out(Y), .gate(A));
  Transistor #(.\type ("n")) transistor_2 (.in(1'b0), .out(Y), .gate(undriven));
endmodule

module cmos_nand (
  input  A,
  input  B,
  output Y
);

  wire transistor_3_out, transistor_4_out, undriven, undriven_2;

  // Transistor #(.\type ("p")) transistor_1: pin names not known; wires that end beside it: A, Y
  Transistor #(.\type ("n")) transistor_2 (.in(transistor_3_out), .out(Y), .gate(undriven));
  Transistor #(.\type ("n")) transistor_3 (.in(1'b0), .out(transistor_3_out), .gate(undriven_2));
  Transistor #(.\type ("p")) transistor_4 (.in(1'b1), .out(transistor_4_out), .gate(B));
endmodule

module tgate_mux (
  input  S,
  input  D0,
  input  D1,
  output Y
);

  wire not_1_out, transmission_1_p1, transmission_1_p2, transmission_1_p7, undriven;

  not not_1 (not_1_out, undriven);
  // Transmission_Gate transmission_1: pin names not known; wires that end beside it: transmission_1_p1, transmission_1_p2, D1, transmission_1_p1, transmission_1_p2, Y, transmission_1_p7
  // Transmission_Gate transmission_2: pin names not known; wires that end beside it: D0, S, not_1_out, transmission_1_p7
endmodule

module pseudo_nor (
  input  A,
  input  B,
  output Y
);

  wire transistor_2_out;

  // Transistor #(.\type ("n")) transistor_1: pin names not known; wires that end beside it: A, Y
  Transistor #(.\type ("n")) transistor_2 (.in(1'b0), .out(transistor_2_out), .gate(B));
  // Pull_Resistor #(.pull(1)) pull_resistor_1: pin names not known
endmodule
