// Logisim project compare_minmax.circ as structural Verilog: 6 circuits, main circuit minmax8
module dp_compare_stage (
  input  LTin,
  input  EQin,
  input  GTin,
  input  A,
  input  B,
  output LTout,
  output EQout,
  output GTout
);

  wire and_1_out, and_2_out, and_3_out, and_4_out, not_1_out, not_2_out, not_3_out, undriven, undriven_2,
       undriven_3, undriven_4, undriven_5, undriven_6, xor_1_out;

  xor xor_1 (xor_1_out, undriven_2, undriven_4);
  not not_1 (not_1_out, undriven);
  not not_2 (not_2_out, undriven_3);
  not not_3 (not_3_out, xor_1_out);
  and and_1 (and_1_out, not_1_out, B);
  and and_2 (and_2_out, A, not_2_out);
  and and_3 (and_3_out, undriven_5, and_1_out);
  and and_4 (and_4_out, undriven_6, and_2_out);
  and and_5 (EQout, EQin, not_3_out);
  or or_1 (LTout, LTin, and_3_out);
  or or_2 (GTout, GTin, and_4_out);
endmodule

module dp_mux2 (
  input  D0,
  input  D1,
  input  S,
  output Y
);

  wire and_1_out, and_2_out, not_1_out, undriven;

  not not_1 (not_1_out, undriven);
  and and_1 (and_1_out, D1, S);
  and and_2 (and_2_out, D0, not_1_out);
  or or_1 (Y, and_2_out, and_1_out);
endmodule

module compare8 (
  input  [7:0] A,
  input  [7:0] B,
  output LT,
  output EQ,
  output GT
);

  wire bit1_eqout, bit1_gtout, bit1_ltout, bit2_eqout, bit2_gtout, bit2_ltout, bit3_eqout, bit3_gtout,
       bit3_ltout, bit4_eqout, bit4_gtout, bit4_ltout, bit5_eqout, bit5_gtout, bit5_ltout, bit6_eqout,
       bit6_gtout, bit6_ltout, bit7_eqout, bit7_gtout, bit7_ltout;

  dp_compare_stage bit7 (
    .LTin(1'b0), .EQin(1'b1), .GTin(1'b0), .A(A[7]), .B(B[7]), .LTout(bit7_ltout), .EQout(bit7_eqout),
    .GTout(bit7_gtout));
  dp_compare_stage bit6 (
    .LTin(bit7_ltout), .EQin(bit7_eqout), .GTin(bit7_gtout), .A(A[6]), .B(B[6]), .LTout(bit6_ltout),
    .EQout(bit6_eqout), .GTout(bit6_gtout));
  dp_compare_stage bit5 (
    .LTin(bit6_ltout), .EQin(bit6_eqout), .GTin(bit6_gtout), .A(A[5]), .B(B[5]), .LTout(bit5_ltout),
    .EQout(bit5_eqout), .GTout(bit5_gtout));
  dp_compare_stage bit4 (
    .LTin(bit5_ltout), .EQin(bit5_eqout), .GTin(bit5_gtout), .A(A[4]), .B(B[4]), .LTout(bit4_ltout),
    .EQout(bit4_eqout), .GTout(bit4_gtout));
  dp_compare_stage bit3 (
    .LTin(bit4_ltout), .EQin(bit4_eqout), .GTin(bit4_gtout), .A(A[3]), .B(B[3]), .LTout(bit3_ltout),
    .EQout(bit3_eqout), .GTout(bit3_gtout));
  dp_compare_stage bit2 (
    .LTin(bit3_ltout), .EQin(bit3_eqout), .GTin(bit3_gtout), .A(A[2]), .B(B[2]), .LTout(bit2_ltout),
    .EQout(bit2_eqout), .GTout(bit2_gtout));
  dp_compare_stage bit1 (
    .LTin(bit2_ltout), .EQin(bit2_eqout), .GTin(bit2_gtout), .A(A[1]), .B(B[1]), .LTout(bit1_ltout),
    .EQout(bit1_eqout), .GTout(bit1_gtout));
  dp_compare_stage bit0 (
    .LTin(bit1_ltout), .EQin(bit1_eqout), .GTin(bit1_gtout), .A(A[0]), .B(B[0]), .LTout(LT), .EQout(EQ),
    .GTout(GT));

  // Notes on the sheet:
  //   8-bit unsigned magnitude comparator
endmodule

module minmax8_compare (
  input  [7:0] A,
  input  [7:0] B,
  output LT,
  output EQ,
  output GT
);

  wire bit1_eqout, bit1_gtout, bit1_ltout, bit2_eqout, bit2_gtout, bit2_ltout, bit3_eqout, bit3_gtout,
       bit3_ltout, bit4_eqout, bit4_gtout, bit4_ltout, bit5_eqout, bit5_gtout, bit5_ltout, bit6_eqout,
       bit6_gtout, bit6_ltout, bit7_eqout, bit7_gtout, bit7_ltout;

  dp_compare_stage bit7 (
    .LTin(1'b0), .EQin(1'b1), .GTin(1'b0), .A(A[7]), .B(B[7]), .LTout(bit7_ltout), .EQout(bit7_eqout),
    .GTout(bit7_gtout));
  dp_compare_stage bit6 (
    .LTin(bit7_ltout), .EQin(bit7_eqout), .GTin(bit7_gtout), .A(A[6]), .B(B[6]), .LTout(bit6_ltout),
    .EQout(bit6_eqout), .GTout(bit6_gtout));
  dp_compare_stage bit5 (
    .LTin(bit6_ltout), .EQin(bit6_eqout), .GTin(bit6_gtout), .A(A[5]), .B(B[5]), .LTout(bit5_ltout),
    .EQout(bit5_eqout), .GTout(bit5_gtout));
  dp_compare_stage bit4 (
    .LTin(bit5_ltout), .EQin(bit5_eqout), .GTin(bit5_gtout), .A(A[4]), .B(B[4]), .LTout(bit4_ltout),
    .EQout(bit4_eqout), .GTout(bit4_gtout));
  dp_compare_stage bit3 (
    .LTin(bit4_ltout), .EQin(bit4_eqout), .GTin(bit4_gtout), .A(A[3]), .B(B[3]), .LTout(bit3_ltout),
    .EQout(bit3_eqout), .GTout(bit3_gtout));
  dp_compare_stage bit2 (
    .LTin(bit3_ltout), .EQin(bit3_eqout), .GTin(bit3_gtout), .A(A[2]), .B(B[2]), .LTout(bit2_ltout),
    .EQout(bit2_eqout), .GTout(bit2_gtout));
  dp_compare_stage bit1 (
    .LTin(bit2_ltout), .EQin(bit2_eqout), .GTin(bit2_gtout), .A(A[1]), .B(B[1]), .LTout(bit1_ltout),
    .EQout(bit1_eqout), .GTout(bit1_gtout));
  dp_compare_stage bit0 (
    .LTin(bit1_ltout), .EQin(bit1_eqout), .GTin(bit1_gtout), .A(A[0]), .B(B[0]), .LTout(LT), .EQout(EQ),
    .GTout(GT));

  // Notes on the sheet:
  //   8-bit unsigned magnitude comparator
endmodule

module minmax8_mux (
  input  [7:0] D0,
  input  [7:0] D1,
  input  S,
  output [7:0] Y
);

  wire undriven, undriven_2, undriven_3, undriven_4, undriven_5, undriven_6, undriven_7;

  dp_mux2 bit7 (.D0(D0[7]), .D1(D1[7]), .S(S), .Y(Y[7]));
  dp_mux2 bit6 (.D0(D0[6]), .D1(D1[6]), .S(undriven), .Y(Y[6]));
  dp_mux2 bit5 (.D0(D0[5]), .D1(D1[5]), .S(undriven_2), .Y(Y[5]));
  dp_mux2 bit4 (.D0(D0[4]), .D1(D1[4]), .S(undriven_3), .Y(Y[4]));
  dp_mux2 bit3 (.D0(D0[3]), .D1(D1[3]), .S(undriven_4), .Y(Y[3]));
  dp_mux2 bit2 (.D0(D0[2]), .D1(D1[2]), .S(undriven_5), .Y(Y[2]));
  dp_mux2 bit1 (.D0(D0[1]), .D1(D1[1]), .S(undriven_6), .Y(Y[1]));
  dp_mux2 bit0 (.D0(D0[0]), .D1(D1[0]), .S(undriven_7), .Y(Y[0]));

  // Notes on the sheet:
  //   8-bit 2:1 selector
endmodule

module minmax8 (
  input  [7:0] A,
  input  [7:0] B,
  output [7:0] MIN,
  output [7:0] MAX
);

  wire A_LT_B, compare_eq, compare_gt;

  minmax8_compare compare (.A(A), .B(B), .LT(A_LT_B), .EQ(compare_eq), .GT(compare_gt));
  // Probe on compare_eq
  // Probe on compare_gt
  minmax8_mux minimum (.D0(B), .D1(A), .S(A_LT_B), .Y(MIN));
  minmax8_mux maximum (.D0(A), .D1(B), .S(A_LT_B), .Y(MAX));

  // Other names for the same wires on the sheet: A_BUS[7:0] = A; B_BUS[7:0] = B

  // Notes on the sheet:
  //   minimum / maximum of two 8-bit unsigned values
  //   compare
  //   select minimum
  //   select maximum
endmodule
