// Logisim project decoder3to8.circ as structural Verilog: 1 circuit, main circuit decoder3to8
module decoder3to8 (
  input  A2,
  input  A1,
  input  A0,
  output Y0,
  output Y1,
  output Y2,
  output Y3,
  output Y4,
  output Y5,
  output Y6,
  output Y7
);

  wire not_1_out, not_2_out, not_3_out, undriven, undriven_2, undriven_3, undriven_4, undriven_5, undriven_6,
       undriven_7, undriven_8, undriven_9, undriven_10, undriven_11, undriven_12, undriven_13, undriven_14,
       undriven_15, undriven_16, undriven_17, undriven_18, undriven_19, undriven_20, undriven_21;

  not not_1 (not_1_out, undriven_2);
  not not_2 (not_2_out, undriven_4);
  not not_3 (not_3_out, undriven_6);
  and and_1 (Y7, undriven, undriven_3, undriven_5);
  and and_2 (Y0, undriven_7, undriven_10, undriven_13);
  and and_3 (Y1, undriven_8, undriven_11, undriven_16);
  and and_4 (Y2, undriven_9, undriven_18, undriven_14);
  and and_5 (Y3, not_1_out, undriven_19, undriven_17);
  and and_6 (Y4, undriven_20, undriven_12, undriven_15);
  and and_7 (Y5, undriven_21, not_2_out, A0);
  and and_8 (Y6, A2, A1, not_3_out);
endmodule
