// Logisim project full_adder.circ as structural Verilog: 1 circuit, main circuit full_adder
module full_adder (
  input  A,
  input  B,
  input  Cin,
  output S,
  output Cout
);

  wire and_1_out, and_2_out, undriven, undriven_2, undriven_3, undriven_4, xor_1_out;

  xor xor_1 (xor_1_out, undriven, undriven_2);
  and and_1 (and_1_out, A, B);
  xor xor_2 (S, undriven_3, undriven_4);
  and and_2 (and_2_out, Cin, xor_1_out);
  or or_1 (Cout, and_1_out, and_2_out);
endmodule
