// Logisim project mux8.circ as structural Verilog: 2 circuits, main circuit mux8
module dp_mux2 (
  input  D0,
  input  D1,
  input  S,
  output Y
);

  wire and_1_out, and_2_out, not_1_out, undriven;

  not not_1 (not_1_out, undriven);
  and and_1 (and_1_out, D1, S);
  and and_2 (and_2_out, D0, not_1_out);
  or or_1 (Y, and_2_out, and_1_out);
endmodule

module mux8 (
  input  [7:0] D0,
  input  [7:0] D1,
  input  S,
  output [7:0] Y
);

  wire undriven, undriven_2, undriven_3, undriven_4, undriven_5, undriven_6, undriven_7;

  dp_mux2 bit7 (.D0(D0[7]), .D1(D1[7]), .S(S), .Y(Y[7]));
  dp_mux2 bit6 (.D0(D0[6]), .D1(D1[6]), .S(undriven), .Y(Y[6]));
  dp_mux2 bit5 (.D0(D0[5]), .D1(D1[5]), .S(undriven_2), .Y(Y[5]));
  dp_mux2 bit4 (.D0(D0[4]), .D1(D1[4]), .S(undriven_3), .Y(Y[4]));
  dp_mux2 bit3 (.D0(D0[3]), .D1(D1[3]), .S(undriven_4), .Y(Y[3]));
  dp_mux2 bit2 (.D0(D0[2]), .D1(D1[2]), .S(undriven_5), .Y(Y[2]));
  dp_mux2 bit1 (.D0(D0[1]), .D1(D1[1]), .S(undriven_6), .Y(Y[1]));
  dp_mux2 bit0 (.D0(D0[0]), .D1(D1[0]), .S(undriven_7), .Y(Y[0]));

  // Notes on the sheet:
  //   8-bit 2:1 selector
endmodule
